// Logisim project counter.circ as structural Verilog: 7 circuits, main circuit main
module main (
  output b0,
  output b1,
  output b2,
  output b3,
  output b4
);

  wire is_17_1_q, t_out;

  Clock t (.out(t_out));
  counter_32 counter_32_1 (.i(t_out), .R(is_17_1_q), .b0(b0), .b1(b1), .b2(b2), .b3(b3), .b4(b4));
  is_17 is_17_1 (.b0(b0), .b1(b1), .b2(b2), .b3(b3), .b4(b4), .Q(is_17_1_q));
endmodule

module RS_trigger (
  input  R,
  input  S,
  output Q,
  output Q_neg
);

  wire nor_2_out, por_1_out;

  POR por_1 (.out(por_1_out));
  nor nor_1 (Q, R, Q_neg);
  nor nor_2 (nor_2_out, Q, S);
  or or_1 (Q_neg, nor_2_out, por_1_out);
endmodule

module D_trigger (
  input  D,
  input  C,
  output Q,
  output Q_neg
);

  wire and_1_out, and_2_out;

  and and_1 (and_1_out, ~D, C);  // AND_Gate
  and and_2 (and_2_out, D, C);
  RS_trigger rs_trigger_1 (.R(and_1_out), .S(and_2_out), .Q(Q), .Q_neg(Q_neg));

  // Notes on the sheet:
  //   C: initial=0x1
endmodule

module T_trigger (
  input  T,
  output Q,
  output Q_neg
);

  wire d_trigger_1_q, not_1_out;

  not not_1 (not_1_out, T);
  D_trigger d_trigger_1 (.D(Q_neg), .C(not_1_out), .Q(d_trigger_1_q));  // open: Q_neg
  D_trigger d_trigger_2 (.D(d_trigger_1_q), .C(T), .Q(Q), .Q_neg(Q_neg));
endmodule

module Reset_T_trigger (
  input  T,
  input  R,
  output Q,
  output Q_neg
);

  wire and_1_out, and_2_out, d_trigger_1_q, not_1_out, or_1_out, or_2_out;

  not not_1 (not_1_out, T);
  and and_1 (and_1_out, Q_neg, ~R);  // AND_Gate
  or or_1 (or_1_out, not_1_out, R);
  D_trigger d_trigger_1 (.D(and_1_out), .C(or_1_out), .Q(d_trigger_1_q));  // open: Q_neg
  and and_2 (and_2_out, ~R, d_trigger_1_q);  // AND_Gate
  or or_2 (or_2_out, R, T);
  D_trigger d_trigger_2 (.D(and_2_out), .C(or_2_out), .Q(Q), .Q_neg(Q_neg));
endmodule

module counter_32 (
  input  i,
  input  R,
  output b0,
  output b1,
  output b2,
  output b3,
  output b4
);

  wire reset_t_trigger_1_q_neg, reset_t_trigger_2_q_neg, reset_t_trigger_3_q_neg, reset_t_trigger_4_q_neg;

  Reset_T_trigger reset_t_trigger_1 (.T(i), .R(R), .Q(b0), .Q_neg(reset_t_trigger_1_q_neg));
  Reset_T_trigger reset_t_trigger_2 (.T(reset_t_trigger_1_q_neg), .R(R), .Q(b1), .Q_neg(reset_t_trigger_2_q_neg));
  Reset_T_trigger reset_t_trigger_3 (.T(reset_t_trigger_2_q_neg), .R(R), .Q(b2), .Q_neg(reset_t_trigger_3_q_neg));
  Reset_T_trigger reset_t_trigger_4 (.T(reset_t_trigger_3_q_neg), .R(R), .Q(b3), .Q_neg(reset_t_trigger_4_q_neg));
  Reset_T_trigger reset_t_trigger_5 (.T(reset_t_trigger_4_q_neg), .R(R), .Q(b4));  // open: Q_neg
endmodule

module is_17 (
  input  b0,
  input  b1,
  input  b2,
  input  b3,
  input  b4,
  output Q
);

  and and_1 (Q, b0, ~b1, ~b2, ~b3, b4);  // AND_Gate
endmodule
