// Logisim project lfsr.circ as structural Verilog: 4 circuits, main circuit main
module main (
  input  in_1,
  input  S,
  output out_3
);

  wire b1_q, b2_q, b3_q, b4_q, b5_q, b6_q, b7_q, b8_q, b9_q, b10_q, b11_q, xor_1_out, xor_2_out, xor_3_out,
       xor_4_out;

  xor xor_1 (xor_1_out, out_3, in_1);
  D_async b11 (.D(xor_1_out), .C(S), .Q(b11_q));  // open: Q_neg
  xor xor_2 (xor_2_out, out_3, b11_q);
  D_async b10 (.D(xor_2_out), .C(S), .Q(b10_q));  // open: Q_neg
  D_async b9 (.D(b10_q), .C(S), .Q(b9_q));  // open: Q_neg
  D_async b8 (.D(b9_q), .C(S), .Q(b8_q));  // open: Q_neg
  xor xor_3 (xor_3_out, out_3, b8_q);
  D_async b7 (.D(xor_3_out), .C(S), .Q(b7_q));  // open: Q_neg
  D_async b6 (.D(b7_q), .C(S), .Q(b6_q));  // open: Q_neg
  xor xor_4 (xor_4_out, out_3, b6_q);
  D_async b5 (.D(xor_4_out), .C(S), .Q(b5_q));  // open: Q_neg
  D_async b4 (.D(b5_q), .C(S), .Q(b4_q));  // open: Q_neg
  D_async b3 (.D(b4_q), .C(S), .Q(b3_q));  // open: Q_neg
  D_async b2 (.D(b3_q), .C(S), .Q(b2_q));  // open: Q_neg
  D_async b1 (.D(b2_q), .C(S), .Q(b1_q));  // open: Q_neg
  D_async b0 (.D(b1_q), .C(S), .Q(out_3));  // open: Q_neg
endmodule

module RS_trigger (
  input  R,
  input  S,
  output Q,
  output Q_neg
);

  wire nor_2_out, por_1_out;

  POR por_1 (.out(por_1_out));
  nor nor_1 (Q, R, Q_neg);
  nor nor_2 (nor_2_out, Q, S);
  or or_1 (Q_neg, nor_2_out, por_1_out);
endmodule

module D_trigger (
  input  D,
  input  C,
  output Q,
  output Q_neg
);

  wire and_1_out, and_2_out;

  and and_1 (and_1_out, ~D, C);  // AND_Gate
  and and_2 (and_2_out, D, C);
  RS_trigger rs_trigger_1 (.R(and_1_out), .S(and_2_out), .Q(Q), .Q_neg(Q_neg));

  // Notes on the sheet:
  //   C: initial=0x1
endmodule

module D_async (
  input  D,
  input  C,
  output Q,
  output Q_neg
);

  wire d_trigger_1_q, not_1_out;

  not not_1 (not_1_out, C);
  D_trigger d_trigger_1 (.D(D), .C(C), .Q(d_trigger_1_q));  // open: Q_neg
  D_trigger d_trigger_2 (.D(d_trigger_1_q), .C(not_1_out), .Q(Q), .Q_neg(Q_neg));
endmodule
